// Digital circuit half-adder.dig as structural Verilog
module half_adder (
  input  in_3,
  input  in_4,
  output out_1,
  output out_2
);

  xor xor_1 (out_1, in_3, in_4);
  and and_1 (out_2, in_3, in_4);
endmodule
